// Logisim project laba_3.circ as structural Verilog: 5 circuits, main circuit main
module main (
  input  P_in,
  input  a,
  input  b,
  input  [7:0] in_4,
  input  [2:0] in_5,
  output a_b,
  output P_out
);

  wire and_1_out, and_2_out, xor_1_out;
  wire [7:0] shifter_1_out;

  // Probe on in_4
  // Probe on in_4
  xor xor_1 (xor_1_out, a, b);
  and and_1 (and_1_out, b, a);
  Shifter #(.shift("ar")) shifter_1 (.in(in_4), .\dist (in_5), .out(shifter_1_out));
  xor xor_2 (a_b, P_in, xor_1_out);
  and and_2 (and_2_out, xor_1_out, P_in);
  // Probe on shifter_1_out
  or or_1 (P_out, and_2_out, and_1_out);

  // Notes on the sheet:
  //   Сумматор с битом переноса
endmodule

module Summator (
  input  [7:0] a,
  input  in_2,
  input  [7:0] b,
  output out_4,
  output [7:0] out_5
);

  wire SUM0_p_out, SUM1_p_out, SUM2_p_out, SUM3_p_out, SUM4_p_out, SUM5_p_out, SUM6_p_out;

  main SUM0 (.P_in(in_2), .a(a[0]), .b(b[0]), .a_b(out_5[0]), .P_out(SUM0_p_out));  // open: in_4, in_5
  main SUM1 (.P_in(SUM0_p_out), .a(a[1]), .b(b[1]), .a_b(out_5[1]), .P_out(SUM1_p_out));  // open: in_4, in_5
  main SUM2 (.P_in(SUM1_p_out), .a(a[2]), .b(b[2]), .a_b(out_5[2]), .P_out(SUM2_p_out));  // open: in_4, in_5
  main SUM3 (.P_in(SUM2_p_out), .a(a[3]), .b(b[3]), .a_b(out_5[3]), .P_out(SUM3_p_out));  // open: in_4, in_5
  main SUM4 (.P_in(SUM3_p_out), .a(a[4]), .b(b[4]), .a_b(out_5[4]), .P_out(SUM4_p_out));  // open: in_4, in_5
  main SUM5 (.P_in(SUM4_p_out), .a(a[5]), .b(b[5]), .a_b(out_5[5]), .P_out(SUM5_p_out));  // open: in_4, in_5
  main SUM6 (.P_in(SUM5_p_out), .a(a[6]), .b(b[6]), .a_b(out_5[6]), .P_out(SUM6_p_out));  // open: in_4, in_5
  main SUM7 (.P_in(SUM6_p_out), .a(a[7]), .b(b[7]), .a_b(out_5[7]), .P_out(out_4));  // open: in_4, in_5
endmodule

module Vichitator (
  input  [7:0] a,
  input  in_2,
  input  [7:0] b,
  output out_4,
  output [7:0] out_5
);

  wire SUM0_p_out, SUM1_p_out, SUM2_p_out, SUM3_p_out, SUM4_p_out, SUM5_p_out, SUM6_p_out, SUM7_p_out;
  wire [7:0] inv_1_out;

  INV inv_1 (.INVERT(in_2), .IN(b), .OUT(inv_1_out));
  main SUM0 (.P_in(in_2), .a(a[0]), .b(inv_1_out[0]), .a_b(out_5[0]), .P_out(SUM0_p_out));  // open: in_4, in_5
  main SUM1 (.P_in(SUM0_p_out), .a(a[1]), .b(inv_1_out[1]), .a_b(out_5[1]), .P_out(SUM1_p_out));  // open: in_4, in_5
  main SUM2 (.P_in(SUM1_p_out), .a(a[2]), .b(inv_1_out[2]), .a_b(out_5[2]), .P_out(SUM2_p_out));  // open: in_4, in_5
  main SUM3 (.P_in(SUM2_p_out), .a(a[3]), .b(inv_1_out[3]), .a_b(out_5[3]), .P_out(SUM3_p_out));  // open: in_4, in_5
  main SUM4 (.P_in(SUM3_p_out), .a(a[4]), .b(inv_1_out[4]), .a_b(out_5[4]), .P_out(SUM4_p_out));  // open: in_4, in_5
  main SUM5 (.P_in(SUM4_p_out), .a(a[5]), .b(inv_1_out[5]), .a_b(out_5[5]), .P_out(SUM5_p_out));  // open: in_4, in_5
  main SUM6 (.P_in(SUM5_p_out), .a(a[6]), .b(inv_1_out[6]), .a_b(out_5[6]), .P_out(SUM6_p_out));  // open: in_4, in_5
  main SUM7 (.P_in(SUM6_p_out), .a(a[7]), .b(inv_1_out[7]), .a_b(out_5[7]), .P_out(SUM7_p_out));  // open: in_4, in_5
  xor xor_1 (out_4, SUM7_p_out, in_2);

  // Other names for the same wires on the sheet: Выч = in_2
endmodule

module INV (
  input  INVERT,
  input  [7:0] IN,
  output [7:0] OUT
);

  xor xor_1 (OUT[7], IN[7], INVERT);
  xor xor_2 (OUT[6], IN[6], INVERT);
  xor xor_3 (OUT[5], IN[5], INVERT);
  xor xor_4 (OUT[4], IN[4], INVERT);
  xor xor_5 (OUT[3], IN[3], INVERT);
  xor xor_6 (OUT[2], IN[2], INVERT);
  xor xor_7 (OUT[1], IN[1], INVERT);
  xor xor_8 (OUT[0], IN[0], INVERT);
endmodule

module Umnozjator (
  input  [3:0] A,
  input  [3:0] B,
  output [7:0] C
);

  wire and_1_out, and_2_out, and_3_out, and_4_out, and_5_out, and_6_out, and_7_out, and_8_out, and_9_out,
       and_10_out, and_11_out, and_12_out, and_13_out, and_14_out, and_15_out, main_2_a_b, main_2_p_out,
       main_3_a_b, main_3_p_out, main_4_a_b, main_4_p_out, main_5_p1, main_5_p5, main_5_p6, main_6_p_out,
       main_7_p_out, main_8_a_b, main_8_p_out, main_9_p5, main_9_p6, main_10_p3, main_12_p1;

  and and_1 (and_1_out, A[3], B[1]);
  and and_2 (and_2_out, A[3], B[2]);
  and and_3 (and_3_out, A[3], B[3]);
  main main_1 (.P_in(main_6_p_out), .a(and_3_out), .b(main_3_p_out), .a_b(C[6]), .P_out(C[7]));  // open: in_4, in_5
  main main_2 (
    .P_in(main_4_p_out), .a(1'b0), .b(and_1_out), .a_b(main_2_a_b), .P_out(main_2_p_out));  // open: in_4, in_5
  and and_4 (and_4_out, A[2], B[2]);
  main main_3 (
    .P_in(main_5_p1), .a(and_2_out), .b(main_2_p_out), .a_b(main_3_a_b), .P_out(main_3_p_out));  // open: in_4, in_5
  and and_5 (and_5_out, A[3], B[0]);
  and and_6 (and_6_out, A[2], B[1]);
  main main_4 (
    .P_in(main_8_p_out), .a(and_5_out), .b(and_6_out), .a_b(main_4_a_b), .P_out(main_4_p_out));  // open: in_4, in_5
  // main main_5: pin names not known; wires that end beside it: main_5_p1, main_2_a_b, main_5_p1, and_4_out, main_5_p5, main_5_p6
  and and_7 (and_7_out, A[2], B[3]);
  main main_6 (
    .P_in(main_7_p_out), .a(and_7_out), .b(main_3_a_b), .a_b(C[5]), .P_out(main_6_p_out));  // open: in_4, in_5
  and and_8 (and_8_out, A[1], B[1]);
  and and_9 (and_9_out, A[1], B[2]);
  and and_10 (and_10_out, A[1], B[3]);
  main main_7 (.P_in(main_12_p1), .a(and_10_out), .b(main_5_p5), .a_b(C[4]), .P_out(main_7_p_out));  // open: in_4, in_5
  and and_11 (and_11_out, A[2], B[0]);
  main main_8 (
    .P_in(main_10_p3), .a(and_11_out), .b(and_8_out), .a_b(main_8_a_b), .P_out(main_8_p_out));  // open: in_4, in_5
  and and_12 (and_12_out, A[0], B[2]);
  // main main_9: pin names not known; wires that end beside it: main_5_p6, main_4_a_b, main_5_p6, and_9_out, main_9_p5, main_9_p6
  and and_13 (and_13_out, A[1], B[0]);
  and and_14 (and_14_out, A[0], B[1]);
  // main main_10: pin names not known; wires that end beside it: and_14_out, and_14_out, main_10_p3, and_13_out, C[1], 1'b0
  // main main_11: pin names not known; wires that end beside it: main_9_p6, main_8_a_b, main_9_p6, and_12_out, C[2], 1'b0
  and and_15 (and_15_out, A[0], B[3]);
  // main main_12: pin names not known; wires that end beside it: main_12_p1, main_9_p5, main_12_p1, and_15_out, C[3], 1'b0
  and and_16 (C[0], A[0], B[0]);
endmodule
